# Fritzing sketch Schematic (saved by Fritzing 0.9.3b)
circuit board: 6.88566cm x 5.36311cm
breadboards: 1

parts:
  1 = Pushbutton [package=THT]
  2 = Pushbutton [package=THT]
  3 = Pushbutton [package=THT]
  4 = Pushbutton [package=THT]
  R4 = Resistor [tolerance=±5% resistance=220 package=THT]
  LED5 = RGB LED (com. cathode, rgb) [package="5 mm [THT]"]
  Bauteil1 = Arduino Mega 2560 (Rev3)
  LED6 = RGB LED (com. cathode, rgb) [package="5 mm [THT]"]
  LED7 = RGB LED (com. cathode, rgb) [package="5 mm [THT]"]
  LED8 = RGB LED (com. cathode, rgb) [package="5 mm [THT]"]

nets:
  N1: 1.leg0, Bauteil1.D4_PWM
  N2: 1.leg1, 2.leg1, 3.leg1, 4.leg1, Bauteil1.D2_PWM
  N3: 2.leg0, Bauteil1.D5_PWM
  N4: 3.leg0, Bauteil1.D6_PWM
  N5: 4.leg0, Bauteil1.D7_PWM
  N6: R4.Pin_0, LED5.red_anode
  N7: R4.Pin_1, Bauteil1.D53
  N8: LED5.common_cathode, Bauteil1.5V, LED6.common_cathode, LED7.common_cathode, LED8.common_cathode
  N9: LED5.green_anode, Bauteil1.GND, LED6.green_anode, LED7.green_anode, LED8.green_anode
  N10: LED5.blue_anode, LED6.red_anode
  N11: LED6.blue_anode, LED7.red_anode
  N12: LED7.blue_anode, LED8.red_anode

notes:
  Svizel_pritula
